# Fritzing sketch WiringLoom (saved by Fritzing 0.9.3b)

parts:
  J6 = Screw terminal - 2 pins [package=THT]
  J7 = female pin header, 9 pins [form="♀ (female)"]
  J8 = female pin header, 6 pins [form="♀ (female)"]
  J9 = shrouded pin header, 26 pins [form="♂ (shrouded male)"]

nets:
  N1: J6.pin1, J9.pin25
  N2: J6.pin2, J9.pin24
  N3: J7.pin1, J9.pin6
  N4: J7.pin2, J9.pin7
  N5: J7.pin3, J9.pin8
  N6: J7.pin4, J9.pin19
  N7: J7.pin5, J9.pin18
  N8: J7.pin6, J9.pin10
  N9: J7.pin7, J9.pin16
  N10: J7.pin8, J7.pin9, J9.pin9, J9.pin17
  N11: J8.pin1, J9.pin1
  N12: J8.pin3, J9.pin2
  N13: J8.pin4, J9.pin3
  N14: J8.pin5, J9.pin4
  N15: J8.pin6, J9.pin5

notes:
  RFID
  Boot Progress PCB
  Amp Power
  Pi
